# Fritzing sketch fridge freezer Fans Control LM317 LM555 (saved by Fritzing 1.0.4)
breadboards: 1

parts:
  J6 = Screw terminal - 2 pins [part_number="12v IN" package=THT]
  D3 = Rectifier Diode [part_number=1N4148 package="300 mil [THT]"]
  D4 = Rectifier Diode [part_number=1N4148 package="300 mil [THT]"]
  J7 = Screw terminal - 2 pins [part_number=Fridge package=THT]
  Q4 = NPN-Transistor [mn=BF393 package="TO92 [THT]"]
  R8 = Resistor [tolerance=±5% power=0.25W resistance=10k package=THT]
  C4 = Electrolytic Capacitor [capacitance=47µF voltage=35V package="200 mil [THT, electrolytic]"]
  U2 = Voltage Regulator - Variable [part_number=LM317 package="TO220 [THT]"]
  U3 = 555 Timer [package="DIP8 [THT]"]
  R10 = Resistor [tolerance=±5% power=0.25W resistance=1k package=THT]
  Q5 = NPN-Transistor [mn=BF393 package="TO92 [THT]"]
  R11 = Resistor [tolerance=±5% power=0.25W resistance=680 package=THT]
  R12 = TRIMPOT [maximum_resistance=5kΩ knob_status=50% power=0.5W package=3386u]
  J10 = Screw terminal - 2 pins [part_number="Upper Fan (100mA max)" package=THT]
  U4 = Voltage Regulator - Variable [part_number=LM317 package="TO220 [THT]"]
  J11 = Screw terminal - 2 pins [part_number="Bottom Fan (100mA max)" package=THT]
  R13 = Resistor [tolerance=±5% power=0.25W resistance=680 package=THT]
  R14 = TRIMPOT [maximum_resistance=5kΩ knob_status=50% power=0.5W package=3386u]
  C11 = Electrolytic Capacitor [capacitance=47µF voltage=35V package="200 mil [THT, electrolytic]"]
  J9 = Screw terminal - 2 pins [part_number=Freezer package=THT]
  C14 = Electrolytic Capacitor [capacitance=22µF voltage=35V package="200 mil [THT, electrolytic]"]
  C15 = Electrolytic Capacitor [capacitance=22µF voltage=35V package="200 mil [THT, electrolytic]"]
  C9 = Electrolytic Capacitor [capacitance=100µF voltage=35V package="200 mil [THT, electrolytic]"]
  R15 = TRIMPOT [maximum_resistance=1MΩ knob_status=50% power=0.5W package=3386u]
  C16 = Ceramic Capacitor [capacitance=10nF voltage=35V package="0603 [SMD, multilayer]"]
  C17 = Ceramic Capacitor [capacitance="100 nF" voltage=35V package="0603 [SMD, multilayer]"]
  C18 = Ceramic Capacitor [capacitance=100nF voltage=35V package="100 mil [THT, multilayer]"]
  C19 = Ceramic Capacitor [capacitance="100 nF" voltage=35V package="0603 [SMD, multilayer]"]
  C20 = Ceramic Capacitor [capacitance="100 nF" voltage=35V package="0603 [SMD, multilayer]"]

nets:
  GND: J6.pin1, J7.pin1, Q4.E, C4.-, U3.Ground, R12.CCW, J10.pin1, J11.pin1, R14.CCW, C11.-, J9.pin1, C14.-, C15.-, C9.-, C16.0, C17.0, C18.0, C19.0, C20.0
  12V: J6.pin2, C4.+, U3.Reset, U3.Vcc_Supply_Voltage, Q5.C, R15.CCW, C17.1
  N1: D3.cathode, D4.cathode, R8.Pin_0, C18.1
  N2: D3.anode, J7.pin2
  N3: D4.anode, J9.pin2
  N4: Q4.B, R8.Pin_1
  N5: Q4.C, U3.Trigger, U3.Threshold, C9.+, R15.WIPER
  N6: U2.ADJ, R11.Pin_0, R12.WIPER
  N7: U2.OUT, R11.Pin_1, J10.pin2, C15.+, C19.1
  N8: U2.IN, Q5.E, U4.IN, C11.+
  N9: U3.Output, R10.Pin_0
  N10: U3.Control_Voltage, C16.1
  N11: R10.Pin_1, Q5.B
  N12: U4.ADJ, R13.Pin_0, R14.WIPER
  N13: U4.OUT, J11.pin2, R13.Pin_1, C14.+, C20.1

notes:
  ORing input signals &
  trigger the monostable
  Retriggerable monostable
  Adjustable voltage supplies
